// Digital circuit 8_ALU.dig as structural Verilog
module _8_ALU (
  input  A0,
  input  A1,
  input  A2,
  input  A3,
  input  A4,
  input  A5,
  input  A6,
  input  A7,
  input  B0,
  input  B1,
  input  B2,
  input  B3,
  input  B4,
  input  B5,
  input  B6,
  input  B7,
  input  K0,
  input  K1,
  input  K2,
  input  Cin,
  output U0,
  output U1,
  output U2,
  output U3,
  output U4,
  output U5,
  output U6,
  output U7,
  output OF,
  output CF
);

  wire _8_fulladder_1_co, _8_mul_1_u0, _8_mul_1_u1, _8_mul_1_u2, _8_mul_1_u3, _8_mul_1_u4, _8_mul_1_u5,
       _8_mul_1_u6, _8_mul_1_u7, _8_mul_2_u0, _8_mul_2_u1, _8_mul_2_u2, _8_mul_2_u3, _8_mul_2_u4,
       _8_mul_2_u5, _8_mul_2_u6, _8_mul_2_u7, _8_mul_3_u0, _8_mul_3_u1, _8_mul_3_u2, _8_mul_3_u3,
       _8_mul_3_u4, _8_mul_3_u5, _8_mul_3_u6, _8_mul_3_u7, not_1_out, not_2_out, not_3_out, not_4_out,
       not_5_out, not_6_out, not_7_out, not_8_out, not_9_out;

  _8_mul _8_mul_1 (
    .A0(B0), .A1(B1), .A2(B2), .A3(B3), .A4(B4), .A5(B5), .A6(B6), .A7(B7), .B0(1'b0), .B1(1'b0), .B2(1'b0),
    .B3(1'b0), .B4(1'b0), .B5(1'b0), .B6(1'b0), .B7(1'b0), .K0(K2), .U0(_8_mul_1_u0), .U1(_8_mul_1_u1),
    .U2(_8_mul_1_u2), .U3(_8_mul_1_u3), .U4(_8_mul_1_u4), .U5(_8_mul_1_u5), .U6(_8_mul_1_u6), .U7(_8_mul_1_u7));
  _8_mul _8_mul_2 (
    .A0(A0), .A1(A1), .A2(A2), .A3(A3), .A4(A4), .A5(A5), .A6(A6), .A7(A7), .B0(1'b0), .B1(1'b0), .B2(1'b0),
    .B3(1'b0), .B4(1'b0), .B5(1'b0), .B6(1'b0), .B7(1'b0), .K0(K1), .U0(_8_mul_2_u0), .U1(_8_mul_2_u1),
    .U2(_8_mul_2_u2), .U3(_8_mul_2_u3), .U4(_8_mul_2_u4), .U5(_8_mul_2_u5), .U6(_8_mul_2_u6), .U7(_8_mul_2_u7));
  not not_1 (not_1_out, _8_mul_1_u0);
  not not_2 (not_2_out, _8_mul_1_u1);
  not not_3 (not_3_out, _8_mul_1_u2);
  not not_4 (not_4_out, _8_mul_1_u3);
  not not_5 (not_5_out, _8_mul_1_u4);
  not not_6 (not_6_out, _8_mul_1_u5);
  not not_7 (not_7_out, _8_mul_1_u6);
  not not_8 (not_8_out, _8_mul_1_u7);
  _8_mul _8_mul_3 (
    .A0(not_1_out), .A1(not_2_out), .A2(not_3_out), .A3(not_4_out), .A4(not_5_out), .A5(not_6_out),
    .A6(not_7_out), .A7(not_8_out), .B0(_8_mul_1_u0), .B1(_8_mul_1_u1), .B2(_8_mul_1_u2), .B3(_8_mul_1_u3),
    .B4(_8_mul_1_u4), .B5(_8_mul_1_u5), .B6(_8_mul_1_u6), .B7(_8_mul_1_u7), .K0(K0), .U0(_8_mul_3_u0),
    .U1(_8_mul_3_u1), .U2(_8_mul_3_u2), .U3(_8_mul_3_u3), .U4(_8_mul_3_u4), .U5(_8_mul_3_u5),
    .U6(_8_mul_3_u6), .U7(_8_mul_3_u7));
  _8_fullAdder _8_fulladder_1 (
    .A0(_8_mul_2_u0), .A1(_8_mul_2_u1), .A2(_8_mul_2_u2), .A3(_8_mul_2_u3), .A4(_8_mul_2_u4),
    .A5(_8_mul_2_u5), .A6(_8_mul_2_u6), .A7(_8_mul_2_u7), .B0(_8_mul_3_u0), .B1(_8_mul_3_u1),
    .B2(_8_mul_3_u2), .B3(_8_mul_3_u3), .B4(_8_mul_3_u4), .B5(_8_mul_3_u5), .B6(_8_mul_3_u6),
    .B7(_8_mul_3_u7), .Cin(Cin), .U0(U0), .U1(U1), .U2(U2), .U3(U3), .U4(U4), .U5(U5), .U6(U6), .U7(U7),
    .Co(_8_fulladder_1_co), .OF(OF));
  not not_9 (not_9_out, _8_fulladder_1_co);
  Multiplexer multiplexer_1 (.sel(K0), .in_0(not_9_out), .in_1(_8_fulladder_1_co), .out(CF));
endmodule

/* Test case:
K0 K1 K2 Cin A0 A1 A2 A3 A4 A5 A6 A7 B0 B1 B2 B3 B4 B5 B6 B7 U0 U1 U2 U3 U4 U5 U6 U7 OF CF
1  0  0  0   1  0  0  0  0  0  0  0  0  0  0  0  0  0  0  1  1  0  0  0  0  0  0  1  0  0
#overflow sum
1  0  0  0   0  0  0  0  0  0  0  1  0  0  0  0  0  0  0  1  X  X  X  X  X  X  X  X  1  1
*/
