// Digital circuit 16_mul.dig as structural Verilog
module _16_mul (
  input  A0,
  input  A1,
  input  A2,
  input  A3,
  input  A4,
  input  A5,
  input  A6,
  input  A7,
  input  A8,
  input  A9,
  input  A10,
  input  A11,
  input  A12,
  input  A13,
  input  A14,
  input  A15,
  input  B0,
  input  B1,
  input  B2,
  input  B3,
  input  B4,
  input  B5,
  input  B6,
  input  B7,
  input  B8,
  input  B9,
  input  B10,
  input  B11,
  input  B12,
  input  B13,
  input  B14,
  input  B15,
  input  K0,
  output U0,
  output U1,
  output U2,
  output U3,
  output U4,
  output U5,
  output U6,
  output U7,
  output U8,
  output U9,
  output U10,
  output U11,
  output U12,
  output U13,
  output U14,
  output U15
);

  _2_mul _2_mul_1 (.A0(A0), .A1(A1), .B0(B0), .B1(B1), .K0(K0), .U0(U0), .U1(U1));
  _2_mul _2_mul_2 (.A0(A2), .A1(A3), .B0(B2), .B1(B3), .K0(K0), .U0(U2), .U1(U3));
  _2_mul _2_mul_3 (.A0(A4), .A1(A5), .B0(B4), .B1(B5), .K0(K0), .U0(U4), .U1(U5));
  _2_mul _2_mul_4 (.A0(A6), .A1(A7), .B0(B6), .B1(B7), .K0(K0), .U0(U6), .U1(U7));
  _2_mul _2_mul_5 (.A0(A8), .A1(A9), .B0(B8), .B1(B9), .K0(K0), .U0(U8), .U1(U9));
  _2_mul _2_mul_6 (.A0(A10), .A1(A11), .B0(B10), .B1(B11), .K0(K0), .U0(U10), .U1(U11));
  _2_mul _2_mul_7 (.A0(A12), .A1(A13), .B0(B12), .B1(B13), .K0(K0), .U0(U12), .U1(U13));
  _2_mul _2_mul_8 (.A0(A14), .A1(A15), .B0(B14), .B1(B15), .K0(K0), .U0(U14), .U1(U15));
endmodule
