// Digital circuit 4_mul.dig as structural Verilog
module _4_mul (
  input  A0,
  input  A1,
  input  A2,
  input  A3,
  input  B0,
  input  B1,
  input  B2,
  input  B3,
  input  K0,
  output U0,
  output U1,
  output U2,
  output U3
);

  _2_mul _2_mul_1 (.A0(A0), .A1(A1), .B0(B0), .B1(B1), .K0(K0), .U0(U0), .U1(U1));
  _2_mul _2_mul_2 (.A0(A2), .A1(A3), .B0(B2), .B1(B3), .K0(K0), .U0(U2), .U1(U3));
endmodule
