// Digital circuit 16_fullAdder.dig as structural Verilog
module _16_fullAdder (
  input  A0,
  input  A1,
  input  A2,
  input  A3,
  input  A4,
  input  A5,
  input  A6,
  input  A7,
  input  A8,
  input  A9,
  input  A10,
  input  A11,
  input  A12,
  input  A13,
  input  A14,
  input  A15,
  input  B0,
  input  B1,
  input  B2,
  input  B3,
  input  B4,
  input  B5,
  input  B6,
  input  B7,
  input  B8,
  input  B9,
  input  B10,
  input  B11,
  input  B12,
  input  B13,
  input  B14,
  input  B15,
  input  Cin,
  output U0,
  output U1,
  output U2,
  output U3,
  output U4,
  output U5,
  output U6,
  output U7,
  output U8,
  output U9,
  output U10,
  output U11,
  output U12,
  output U13,
  output U14,
  output U15,
  output Co
);

  wire _2_fulladder_2_co, _2_fulladder_3_co, _2_fulladder_4_co, _2_fulladder_5_co, _2_fulladder_6_co,
       _2_fulladder_7_co, _2_fulladder_8_co;

  _2_fullAdder _2_fulladder_1 (
    .A0(A14), .A1(A15), .B1(B15), .B0(B14), .Cin(_2_fulladder_2_co), .U0(U14), .U1(U15), .Co(Co));
  _2_fullAdder _2_fulladder_2 (
    .A0(A12), .A1(A13), .B1(B13), .B0(B12), .Cin(_2_fulladder_3_co), .U0(U12), .U1(U13),
    .Co(_2_fulladder_2_co));
  _2_fullAdder _2_fulladder_3 (
    .A0(A10), .A1(A11), .B1(B11), .B0(B10), .Cin(_2_fulladder_4_co), .U0(U10), .U1(U11),
    .Co(_2_fulladder_3_co));
  _2_fullAdder _2_fulladder_4 (
    .A0(A8), .A1(A9), .B1(B9), .B0(B8), .Cin(_2_fulladder_5_co), .U0(U8), .U1(U9), .Co(_2_fulladder_4_co));
  _2_fullAdder _2_fulladder_5 (
    .A0(A6), .A1(A7), .B1(B7), .B0(B6), .Cin(_2_fulladder_6_co), .U0(U6), .U1(U7), .Co(_2_fulladder_5_co));
  _2_fullAdder _2_fulladder_6 (
    .A0(A4), .A1(A5), .B1(B5), .B0(B4), .Cin(_2_fulladder_7_co), .U0(U4), .U1(U5), .Co(_2_fulladder_6_co));
  _2_fullAdder _2_fulladder_7 (
    .A0(A2), .A1(A3), .B1(B3), .B0(B2), .Cin(_2_fulladder_8_co), .U0(U2), .U1(U3), .Co(_2_fulladder_7_co));
  _2_fullAdder _2_fulladder_8 (.A0(A0), .A1(A1), .B1(B1), .B0(B0), .Cin(Cin), .U0(U0), .U1(U1), .Co(_2_fulladder_8_co));
endmodule
