// Digital circuit 2_fullAdder.dig as structural Verilog
module _2_fullAdder (
  input  A0,
  input  A1,
  input  B1,
  input  B0,
  input  Cin,
  output U0,
  output U1,
  output Co
);

  wire fulladder_2_co;

  fullAdder fulladder_1 (.A(A1), .B(B1), .Ci(fulladder_2_co), .S(U1), .Co(Co));
  fullAdder fulladder_2 (.A(A0), .B(B0), .Ci(Cin), .S(U0), .Co(fulladder_2_co));
endmodule
