// Digital circuit 4_fullAdder.dig as structural Verilog
module _4_fullAdder (
  input  A0,
  input  A1,
  input  A2,
  input  A3,
  input  B0,
  input  B1,
  input  B2,
  input  B3,
  input  Cin,
  output U0,
  output U1,
  output U2,
  output U3,
  output Co
);

  wire _2_fulladder_2_co;

  _2_fullAdder _2_fulladder_1 (.A0(A2), .A1(A3), .B1(B3), .B0(B2), .Cin(_2_fulladder_2_co), .U0(U2), .U1(U3), .Co(Co));
  _2_fullAdder _2_fulladder_2 (.A0(A0), .A1(A1), .B1(B1), .B0(B0), .Cin(Cin), .U0(U0), .U1(U1), .Co(_2_fulladder_2_co));
endmodule
