// Digital circuit 2_fullAdder.dig as structural Verilog
module _2_fullAdder (
  input  A0,
  input  A1,
  input  B1,
  input  B0,
  input  Cin,
  output U0,
  output U1,
  output C0,
  output C1
);

  fullAdder fulladder_1 (.A(A1), .B(B1), .Ci(C1), .S(U1), .Co(C0));
  fullAdder fulladder_2 (.A(A0), .B(B0), .Ci(Cin), .S(U0), .Co(C1));
endmodule
