// Digital circuit 8_fullAdder.dig as structural Verilog
module _8_fullAdder (
  input  A0,
  input  A1,
  input  A2,
  input  A3,
  input  A4,
  input  A5,
  input  A6,
  input  A7,
  input  B0,
  input  B1,
  input  B2,
  input  B3,
  input  B4,
  input  B5,
  input  B6,
  input  B7,
  input  Cin,
  output U0,
  output U1,
  output U2,
  output U3,
  output U4,
  output U5,
  output U6,
  output U7,
  output Co,
  output OF
);

  wire _2_fulladder_1_c1, _2_fulladder_2_c0, _2_fulladder_3_c0, _2_fulladder_4_c0;

  xor xor_1 (OF, _2_fulladder_1_c1, Co);
  _2_fullAdder _2_fulladder_1 (
    .A0(A6), .A1(A7), .B1(B7), .B0(B6), .Cin(_2_fulladder_2_c0), .U0(U6), .U1(U7), .C0(Co),
    .C1(_2_fulladder_1_c1));
  _2_fullAdder _2_fulladder_2 (
    .A0(A4), .A1(A5), .B1(B5), .B0(B4), .Cin(_2_fulladder_3_c0), .U0(U4), .U1(U5), .C0(_2_fulladder_2_c0));  // open: C1
  _2_fullAdder _2_fulladder_3 (
    .A0(A2), .A1(A3), .B1(B3), .B0(B2), .Cin(_2_fulladder_4_c0), .U0(U2), .U1(U3), .C0(_2_fulladder_3_c0));  // open: C1
  _2_fullAdder _2_fulladder_4 (
    .A0(A0), .A1(A1), .B1(B1), .B0(B0), .Cin(Cin), .U0(U0), .U1(U1), .C0(_2_fulladder_4_c0));  // open: C1
endmodule
