// Digital circuit fullAdder.dig as structural Verilog
module fullAdder (
  input  A,
  input  B,
  input  Ci,
  output S,
  output Co
);

  wire halfadder_1_r, halfadder_1_s, halfadder_2_r;

  halfAdder halfadder_1 (.A(A), .B(B), .S(halfadder_1_s), .R(halfadder_1_r));
  halfAdder halfadder_2 (.A(Ci), .B(halfadder_1_s), .S(S), .R(halfadder_2_r));
  or or_1 (Co, halfadder_2_r, halfadder_1_r);
endmodule
