// Digital circuit 2_mul.dig as structural Verilog
module _2_mul (
  input  A0,
  input  A1,
  input  B0,
  input  B1,
  input  K0,
  output U0,
  output U1
);

  Multiplexer multiplexer_1 (.sel(K0), .in_0(A0), .in_1(B0), .out(U0));
  Multiplexer multiplexer_2 (.sel(K0), .in_0(A1), .in_1(B1), .out(U1));
endmodule
