// Digital circuit 8_mul.dig as structural Verilog
module _8_mul (
  input  A0,
  input  A1,
  input  A2,
  input  A3,
  input  A4,
  input  A5,
  input  A6,
  input  A7,
  input  B0,
  input  B1,
  input  B2,
  input  B3,
  input  B4,
  input  B5,
  input  B6,
  input  B7,
  input  K0,
  output U0,
  output U1,
  output U2,
  output U3,
  output U4,
  output U5,
  output U6,
  output U7
);

  _2_mul _2_mul_1 (.A0(A0), .A1(A1), .B0(B0), .B1(B1), .K0(K0), .U0(U0), .U1(U1));
  _2_mul _2_mul_2 (.A0(A2), .A1(A3), .B0(B2), .B1(B3), .K0(K0), .U0(U2), .U1(U3));
  _2_mul _2_mul_3 (.A0(A4), .A1(A5), .B0(B4), .B1(B5), .K0(K0), .U0(U4), .U1(U5));
  _2_mul _2_mul_4 (.A0(A6), .A1(A7), .B0(B6), .B1(B7), .K0(K0), .U0(U6), .U1(U7));
endmodule
