// Digital circuit es4.dig as structural Verilog
module es4 (
  input  sensor,
  input  clk,
  output [5:0] length
);

  wire and_1_out, counterx3_1_co, monoimpulsore_1_down, monoimpulsore_1_up, or_1_out, or_2_out, or_3_out,
       or_4_out;
  wire [5:0] counterx3_1_q_0;

  monoimpulsore monoimpulsore_1 (.D(sensor), .clk(clk), .Down(monoimpulsore_1_down), .Up(monoimpulsore_1_up));
  or or_1 (or_1_out, or_3_out, or_4_out);
  or or_2 (or_2_out, or_1_out, monoimpulsore_1_up);
  counterx3 counterx3_1 (
    .Res(monoimpulsore_1_down), .EN(or_2_out), .clk(clk), .L(1'b0), .U_D(1'b1), .I_2(1'b1), .I_1(1'b1),
    .I_0(1'b1), .Q_0(counterx3_1_q_0[0]), .Q_1(counterx3_1_q_0[1]), .Q_2(counterx3_1_q_0[2]),
    .CO(counterx3_1_co));
  or or_3 (or_3_out, counterx3_1_q_0[0], counterx3_1_q_0[1], counterx3_1_q_0[2]);
  and and_1 (and_1_out, or_2_out, counterx3_1_co);
  counterx3 counterx3_2 (
    .Res(monoimpulsore_1_down), .EN(and_1_out), .clk(clk), .L(1'b0), .U_D(1'b1), .I_2(1'b1), .I_1(1'b1),
    .I_0(1'b1), .Q_0(counterx3_1_q_0[3]), .Q_1(counterx3_1_q_0[4]), .Q_2(counterx3_1_q_0[5]));  // open: CO
  or or_4 (or_4_out, counterx3_1_q_0[3], counterx3_1_q_0[4], counterx3_1_q_0[5]);
  // registro #(.generic("bitWidth := 6;")) registro_1: pin names not known; wires that end beside it: monoimpulsore_1_down, counterx3_1_q_0, 1'b0, clk, length
endmodule
