// Digital circuit riscaldamento_esercizio2_pasqua.dig as structural Verilog
module riscaldamento_esercizio2_pasqua (
  input  A,
  input  B,
  input  C,
  input  D,
  output O_A,
  output O_B,
  output O_C,
  output O_D
);

  wire and_2_out, and_3_out, nand_1_out, nand_2_out, nand_3_out;

  nand nand_1 (nand_1_out, B, A);
  and and_1 (O_C, nand_1_out, C);
  and and_2 (and_2_out, nand_1_out, D);
  nand nand_2 (nand_2_out, B, O_C);
  and and_3 (and_3_out, nand_2_out, and_2_out);
  nand nand_3 (nand_3_out, A, O_C);
  and and_4 (O_D, nand_3_out, and_3_out);

  assign O_A = A;
  assign O_B = B;
endmodule

/* Test case:
A B C D O_A O_B O_C O_D
1 1 1 1 1 1 0 0
1 1 0 1 1 1 0 0
1 1 1 0 1 1 0 0
1 0 1 1 1 0 1 0
0 1 1 1 0 1 1 0
0 0 1 1 0 0 1 1
*/
