// Digital circuit FF-D.dig as structural Verilog
module FF_D (
  input  D,
  input  CLK,
  input  PRE,
  input  CLR,
  output Q,
  output Q_2
);

  wire nand_1_out, nand_2_out, nand_3_out, nand_4_out;

  nand nand_1 (nand_1_out, PRE, nand_4_out, nand_2_out);
  nand nand_2 (nand_2_out, nand_1_out, CLR, CLK);
  nand nand_3 (nand_3_out, nand_2_out, CLK, nand_4_out);
  nand nand_4 (nand_4_out, nand_3_out, CLR, D);
  nand nand_5 (Q, PRE, nand_2_out, Q_2);
  nand nand_6 (Q_2, Q, CLR, nand_3_out);

  // Notes on the sheet:
  //   PRE: default 1
  //   CLR: default 1
endmodule
