// Digital circuit counterx3.dig as structural Verilog
module counterx3 (
  input  EN,
  input  Res,
  input  U_D,
  input  L,
  input  I_0,
  input  I_1,
  input  I_2,
  input  clk,
  output Q_0,
  output Q_1,
  output Q_2,
  output CO
);

  wire and_1_out, and_2_out, and_3_out, and_4_out, and_5_out, and_6_out, and_7_out, ff_d_1_q_2,
       multiplexer_1_out, multiplexer_2_out, multiplexer_3_out, multiplexer_4_out, multiplexer_5_out,
       nor_1_out, nor_2_out, not_1_out, reset_1_out, xor_1_out, xor_2_out, xor_3_out;

  xor xor_1 (xor_1_out, Q_0, EN);
  not not_1 (not_1_out, Res);
  Multiplexer multiplexer_1 (.sel(L), .in_0(xor_1_out), .in_1(I_0), .out(multiplexer_1_out));
  and and_1 (and_1_out, not_1_out, multiplexer_1_out);
  FF_D ff_d_1 (.D(and_1_out), .CLK(clk), .PRE(1'b1), .CLR(reset_1_out), .Q(Q_0), .Q_2(ff_d_1_q_2));
  Reset reset_1 (.out(reset_1_out));
  and and_2 (and_2_out, EN, multiplexer_2_out);
  Multiplexer multiplexer_2 (.sel(U_D), .in_0(ff_d_1_q_2), .in_1(Q_0), .out(multiplexer_2_out));
  xor xor_2 (xor_2_out, Q_1, and_2_out);
  Multiplexer multiplexer_3 (.sel(L), .in_0(xor_2_out), .in_1(I_1), .out(multiplexer_3_out));
  and and_3 (and_3_out, not_1_out, multiplexer_3_out);
  FF_D ff_d_2 (.D(and_3_out), .CLK(clk), .PRE(1'b1), .CLR(reset_1_out), .Q(Q_1));  // open: Q_2
  and and_4 (and_4_out, Q_0, Q_1);
  nor nor_1 (nor_1_out, Q_1, Q_0);
  Multiplexer multiplexer_4 (.sel(U_D), .in_0(nor_1_out), .in_1(and_4_out), .out(multiplexer_4_out));
  and and_5 (and_5_out, multiplexer_4_out, EN);
  xor xor_3 (xor_3_out, Q_2, and_5_out);
  Multiplexer multiplexer_5 (.sel(L), .in_0(xor_3_out), .in_1(I_2), .out(multiplexer_5_out));
  and and_6 (and_6_out, not_1_out, multiplexer_5_out);
  FF_D ff_d_3 (.D(and_6_out), .CLK(clk), .PRE(1'b1), .CLR(reset_1_out), .Q(Q_2));  // open: Q_2
  nor nor_2 (nor_2_out, Q_0, Q_2, Q_1);
  and and_7 (and_7_out, Q_0, Q_2, Q_1);
  Multiplexer multiplexer_6 (.sel(U_D), .in_0(nor_2_out), .in_1(and_7_out), .out(CO));
endmodule
