// Digital circuit monoimpulsore.dig as structural Verilog
module monoimpulsore (
  input  D,
  input  clk,
  output Down,
  output Up
);

  wire ff_d_1_q, ff_d_2_q, ff_d_3_q, ff_d_3_q_2, not_1_out, reset_1_out;

  FF_D ff_d_1 (.D(D), .CLK(clk), .PRE(1'b1), .CLR(reset_1_out), .Q(ff_d_1_q));  // open: Q_2
  Reset reset_1 (.out(reset_1_out));
  FF_D ff_d_2 (.D(ff_d_1_q), .CLK(clk), .PRE(1'b1), .CLR(reset_1_out), .Q(ff_d_2_q));  // open: Q_2
  FF_D ff_d_3 (.D(ff_d_2_q), .CLK(clk), .PRE(1'b1), .CLR(reset_1_out), .Q(ff_d_3_q), .Q_2(ff_d_3_q_2));
  not not_1 (not_1_out, ff_d_2_q);
  and and_1 (Down, not_1_out, ff_d_3_q);
  and and_2 (Up, ff_d_2_q, ff_d_3_q_2);
endmodule
