// Digital circuit registro.dig as structural Verilog
module registro (
  input  WE,
  input  [1:0] IN,
  input  RES,
  input  clk,
  output [1:0] Q
);

  wire [1:0] multiplexer_1_out, multiplexer_2_out;

  Multiplexer #(.Bits(2), .generic("this.Bits=args.bitWidth;")) multiplexer_1 (
    .sel(WE), .in_0(Q), .in_1(IN), .out(multiplexer_1_out));
  Multiplexer #(.Bits(2), .generic("this.Bits=args.bitWidth;")) multiplexer_2 (
    .sel(RES), .in_0(multiplexer_1_out), .in_1(2'b00), .out(multiplexer_2_out));
  Register #(.Bits(2), .generic("this.Bits=args.bitWidth;")) register_1 (
    .D(multiplexer_2_out), .C(clk), .en(1'b1), .Q(Q));
endmodule
