// Digital circuit sync.dig as structural Verilog
module sync (
  input  D,
  input  clk,
  output D_sync
);

  wire ff_d_1_q, reset_1_out;

  FF_D ff_d_1 (.D(D), .CLK(clk), .PRE(1'b1), .CLR(reset_1_out), .Q(ff_d_1_q));  // open: Q_2
  Reset reset_1 (.out(reset_1_out));
  FF_D ff_d_2 (.D(ff_d_1_q), .CLK(clk), .PRE(1'b1), .CLR(reset_1_out), .Q(D_sync));  // open: Q_2
endmodule
