// Digital circuit MUX_DEC_ROM.dig as structural Verilog
module MUX_DEC_ROM (
  input  [1:0] BA_3,
  input  [1:0] BA_4,
  input  [1:0] BA_5,
  input  A,
  input  B,
  input  [1:0] BA_6,
  input  [1:0] DC,
  input  [3:0] DCBA,
  output B_A,
  output B_A_2,
  output BA,
  output BA_2,
  output OR,
  output AND,
  output NAND,
  output NOR,
  output EXOR,
  output EQUIVALENCE,
  output [5:0] functions,
  output AND_2,
  output AND_MUX_comp,
  output F_MUX_com,
  output F,
  output D_C_B_A,
  output D_C_BA,
  output D_C_BA_2,
  output D_CB_A,
  output D_CB_A_2,
  output D_CBA,
  output D_CBA_2,
  output DC_B_A,
  output DC_B_A_2,
  output DC_BA,
  output DC_BA_2,
  output DCB_A,
  output DCB_A_2,
  output DCBA_2,
  output D_C_B_A_2,
  output DCBA_3,
  output F_DEC
);

  wire multiplexer_1_out, multiplexer_2_out, multiplexer_3_out, multiplexer_4_out, multiplexer_8_out,
       multiplexer_9_out, or_1_out, or_2_out, or_3_out, or_4_out, or_5_out;

  Multiplexer #(.Selector_Bits(2)) multiplexer_1 (
    .sel(BA_6), .in_0(1'b0), .in_1(1'b1), .in_2(1'b1), .in_3(1'b1), .out(multiplexer_1_out));
  Multiplexer #(.Selector_Bits(2)) multiplexer_2 (
    .sel(BA_6), .in_0(1'b0), .in_1(1'b1), .in_2(1'b1), .in_3(1'b1), .out(multiplexer_2_out));
  Multiplexer #(.Selector_Bits(2)) multiplexer_3 (
    .sel(BA_6), .in_0(1'b0), .in_1(1'b1), .in_2(1'b1), .in_3(1'b1), .out(multiplexer_3_out));
  Multiplexer #(.Selector_Bits(2)) multiplexer_4 (
    .sel(BA_6), .in_0(1'b0), .in_1(1'b1), .in_2(1'b1), .in_3(1'b1), .out(multiplexer_4_out));
  Multiplexer #(.Selector_Bits(4)) multiplexer_5 (
    .sel(DCBA), .in_0(1'b0), .in_1(1'b1), .in_2(1'b1), .in_3(1'b1), .in_4(1'b0), .in_5(1'b1), .in_6(1'b1),
    .in_7(1'b1), .in_8(1'b0), .in_9(1'b1), .in_10(1'b1), .in_11(1'b1), .in_12(1'b0), .in_13(1'b1),
    .in_14(1'b1), .in_15(1'b1), .out(F));
  Multiplexer #(.Selector_Bits(2)) multiplexer_6 (
    .sel(DC), .in_0(multiplexer_1_out), .in_1(multiplexer_2_out), .in_2(multiplexer_3_out),
    .in_3(multiplexer_4_out), .out(F_MUX_com));
  Decoder #(.Selector_Bits(4)) decoder_1 (
    .sel(DCBA), .out_0(D_C_B_A_2), .out_1(D_C_B_A), .out_2(D_C_BA), .out_3(D_C_BA_2), .out_4(D_CB_A),
    .out_5(D_CB_A_2), .out_6(D_CBA), .out_7(D_CBA_2), .out_8(DC_B_A), .out_9(DC_B_A_2), .out_10(DC_BA),
    .out_11(DC_BA_2), .out_12(DCB_A), .out_13(DCB_A_2), .out_14(DCBA_2), .out_15(DCBA_3));
  or or_1 (or_1_out, D_C_BA_2, D_C_BA, D_C_B_A);
  or or_2 (or_2_out, D_CBA_2, D_CBA, D_CB_A_2);
  or or_3 (or_3_out, or_2_out, or_1_out);
  or or_4 (or_4_out, DC_BA_2, DC_BA, DC_B_A_2);
  or or_5 (or_5_out, DCBA_3, DCBA_2, DCB_A_2);
  or or_6 (F_DEC, or_5_out, or_4_out, or_3_out);
  Multiplexer #(.Selector_Bits(2)) multiplexer_7 (
    .sel(BA_5), .in_0(1'b0), .in_1(1'b1), .in_2(1'b1), .in_3(1'b1), .out(AND_2));
  Multiplexer multiplexer_8 (.sel(A), .in_0(1'b0), .in_1(1'b1), .out(multiplexer_8_out));
  Multiplexer multiplexer_9 (.sel(A), .in_0(1'b1), .in_1(1'b1), .out(multiplexer_9_out));
  Multiplexer multiplexer_10 (.sel(B), .in_0(multiplexer_8_out), .in_1(multiplexer_9_out), .out(AND_MUX_comp));
  Decoder #(.Selector_Bits(2)) decoder_2 (.sel(BA_3), .out_0(B_A), .out_1(B_A_2), .out_2(BA), .out_3(AND));
  or or_7 (EQUIVALENCE, AND, B_A);
  ROM #(.Bits(6), .isProgramMemory("true")) rom_1 (.A(BA_4), .sel(1'b1), .D(functions));
  or or_8 (EXOR, BA, B_A_2);
  or or_9 (OR, B_A_2, BA, AND);
  or or_10 (NAND, B_A, B_A_2, BA);

  assign BA_2 = AND;
  assign NOR = B_A;

  // Notes on the sheet:
  //   functions: 2 bit functions
  //   contents of rom_1 (hex, n*v repeats v):
  //   23,1a,1a,18aec
endmodule
