// Digital circuit Toffoli.dig as structural Verilog
module Toffoli (
  input  a_2,
  input  b_2,
  input  z_2,
  output A,
  output B,
  output Z
);

  wire and_1_out;

  and and_1 (and_1_out, a_2, b_2);
  xor xor_1 (Z, and_1_out, z_2);

  assign A = a_2;
  assign B = b_2;
endmodule
